// Logisim project circuit.circ as structural Verilog: 1 circuit, main circuit main
module main (
  input  O1,
  input  O0,
  input  S,
  input  B0,
  input  A0,
  input  B1,
  input  A1,
  output L0,
  output L1,
  output L2,
  output L3,
  output L4,
  output L5,
  output L6,
  output L7,
  output N,
  output B,
  output G,
  output E,
  output L
);

  wire and_1_out, and_2_out, and_3_out, and_4_out, and_5_out, and_6_out, and_7_out, and_8_out, and_9_out,
       and_10_out, and_11_out, and_12_out, and_13_out, and_14_out, and_15_out, and_17_out, and_18_out,
       and_19_out, and_20_out, and_21_out, and_22_out, and_23_out, and_24_out, and_26_out, and_27_out,
       and_28_out, and_29_out, and_30_out, and_31_out, and_32_out, n2_to_4_decoder_x2_74155_1_p2,
       n2_to_4_decoder_x2_74155_1_p4, n2_to_4_decoder_x2_74155_1_p5, n2_to_4_decoder_x2_74155_2_p1,
       n2_to_4_decoder_x2_74155_2_p5, n2_to_4_decoder_x2_74155_2_p7, n2_to_4_decoder_x2_74155_2_p8,
       n2_to_4_decoder_x2_74155_3_p1, n2_to_4_decoder_x2_74155_3_p2, n2_to_4_decoder_x2_74155_3_p4,
       n2_to_4_decoder_x2_74155_3_p5, n2_to_4_decoder_x2_74155_3_p6, n2_to_4_decoder_x2_74155_3_p7,
       n2_to_4_decoder_x2_74155_4_p2, n2_to_4_decoder_x2_74155_4_p3, n2_to_4_decoder_x2_74155_4_p4,
       n2_to_4_decoder_x2_74155_4_p5, n2_to_4_decoder_x2_74155_4_p6, n3_to_8_decoder_74138_1_p2,
       n3_to_8_decoder_74138_1_p4, n3_to_8_decoder_74138_1_p5, n3_to_8_decoder_74138_1_p6,
       n3_to_8_decoder_74138_1_p7, n3_to_8_decoder_74138_1_p8, n3_to_8_decoder_74138_1_p9,
       n3_to_8_decoder_74138_1_p10, n3_to_8_decoder_74138_1_p12, not_1_out, not_2_out, not_3_out, not_4_out,
       not_5_out, not_6_out, not_7_out, not_8_out, not_9_out, not_10_out, not_11_out, not_12_out, not_13_out,
       not_14_out, not_15_out, not_17_out, not_18_out, not_19_out, not_20_out, not_21_out, not_22_out,
       not_26_out, not_27_out, not_28_out, not_29_out, or_1_out, or_2_out, or_4_out, or_9_out, or_11_out,
       or_12_out, or_13_out, or_14_out, or_16_out, or_17_out, or_18_out, xnor_1_out, xnor_2_out, xor_1_out,
       xor_2_out, xor_3_out;

  not not_1 (not_1_out, O1);
  not not_2 (not_2_out, O0);
  not not_3 (not_3_out, S);
  and and_1 (and_1_out, O1, O0);
  and and_2 (and_2_out, and_1_out, S);
  and and_3 (and_3_out, O1, O0);
  and and_4 (and_4_out, and_3_out, not_3_out);
  and and_5 (and_5_out, O1, not_2_out);
  and and_6 (and_6_out, and_5_out, S);
  and and_7 (and_7_out, O1, not_2_out);
  and and_8 (and_8_out, and_7_out, not_3_out);
  and and_9 (and_9_out, not_1_out, O0);
  and and_10 (and_10_out, not_1_out, not_2_out);
  or or_1 (or_1_out, not_6_out, not_18_out);
  or or_2 (or_2_out, or_1_out, not_26_out);
  or or_3 (L0, or_2_out, not_15_out);
  // _2_to_4_Decoder__x2___74155 #(.Facing("south")) 2_to_4_decoder_x2_74155_1: pin names not known; wires that end beside it: A0, n2_to_4_decoder_x2_74155_1_p2, A1, n2_to_4_decoder_x2_74155_1_p4, n2_to_4_decoder_x2_74155_1_p5
  not not_4 (not_4_out, n2_to_4_decoder_x2_74155_1_p5);
  not not_5 (not_5_out, n2_to_4_decoder_x2_74155_1_p4);
  not not_6 (not_6_out, n2_to_4_decoder_x2_74155_1_p2);
  not not_7 (not_7_out, n2_to_4_decoder_x2_74155_2_p1);
  or or_4 (or_4_out, not_5_out, not_20_out);
  or or_5 (L2, or_4_out, not_29_out);
  not not_8 (not_8_out, A1);
  not not_9 (not_9_out, B1);
  not not_10 (not_10_out, A0);
  not not_11 (not_11_out, B0);
  and and_11 (and_11_out, and_8_out, A1);
  not not_12 (not_12_out, and_6_out);
  not not_13 (not_13_out, 1'b1);
  // _2_to_4_Decoder__x2___74155 #(.Facing("south")) 2_to_4_decoder_x2_74155_2: pin names not known; wires that end beside it: n2_to_4_decoder_x2_74155_2_p1, not_12_out, and_6_out, and_11_out, n2_to_4_decoder_x2_74155_2_p5, not_13_out, n2_to_4_decoder_x2_74155_2_p7, n2_to_4_decoder_x2_74155_2_p8, and_8_out
  not not_14 (not_14_out, n2_to_4_decoder_x2_74155_2_p7);
  not not_15 (not_15_out, n2_to_4_decoder_x2_74155_2_p5);
  or or_6 (L4, not_4_out, not_21_out);
  or or_7 (L6, not_7_out, not_22_out);
  not not_16 (n2_to_4_decoder_x2_74155_2_p8, and_8_out);
  xor xor_1 (xor_1_out, B0, A0);
  xor xor_2 (xor_2_out, and_12_out, xor_3_out);
  // _3_to_8_decoder__74138 #(.Facing("south")) 3_to_8_decoder_74138_1: pin names not known; wires that end beside it: xor_1_out, n3_to_8_decoder_74138_1_p2, xor_2_out, n3_to_8_decoder_74138_1_p4, n3_to_8_decoder_74138_1_p5, n3_to_8_decoder_74138_1_p6, n3_to_8_decoder_74138_1_p7, n3_to_8_decoder_74138_1_p8, n3_to_8_decoder_74138_1_p9, n3_to_8_decoder_74138_1_p10, and_4_out, n3_to_8_decoder_74138_1_p12, n3_to_8_decoder_74138_1_p12
  not not_17 (not_17_out, n3_to_8_decoder_74138_1_p7);
  not not_18 (not_18_out, n3_to_8_decoder_74138_1_p2);
  not not_19 (not_19_out, n3_to_8_decoder_74138_1_p4);
  not not_20 (not_20_out, n3_to_8_decoder_74138_1_p6);
  and and_12 (and_12_out, B0, A0);
  xor xor_3 (xor_3_out, B1, A1);
  and and_13 (and_13_out, and_12_out, xor_3_out);
  or or_8 (n3_to_8_decoder_74138_1_p5, and_13_out, and_14_out);
  not not_21 (not_21_out, n3_to_8_decoder_74138_1_p8);
  not not_22 (not_22_out, n3_to_8_decoder_74138_1_p10);
  not not_23 (L5, n3_to_8_decoder_74138_1_p9);
  or or_9 (or_9_out, not_14_out, not_19_out);
  or or_10 (L1, or_9_out, not_27_out);
  and and_14 (and_14_out, B1, A1);
  and and_15 (and_15_out, B1, and_17_out);
  or or_11 (or_11_out, and_15_out, or_12_out);
  not not_24 (n3_to_8_decoder_74138_1_p12, and_4_out);
  and and_16 (N, or_11_out, and_2_out);
  not not_25 (L7, 1'b1);
  and and_17 (and_17_out, B0, not_10_out);
  and and_18 (and_18_out, and_17_out, not_8_out);
  or or_12 (or_12_out, and_18_out, and_20_out);
  and and_19 (and_19_out, and_20_out, not_10_out);
  and and_20 (and_20_out, not_8_out, B1);
  and and_21 (and_21_out, B0, and_20_out);
  or or_13 (or_13_out, and_21_out, or_16_out);
  or or_14 (or_14_out, and_19_out, or_13_out);
  or or_15 (L3, not_17_out, not_28_out);
  and and_22 (and_22_out, A1, not_9_out);
  and and_23 (and_23_out, not_11_out, and_22_out);
  and and_24 (and_24_out, A0, and_22_out);
  or or_16 (or_16_out, and_24_out, and_23_out);
  // _2_to_4_Decoder__x2___74155 #(.Facing("south")) 2_to_4_decoder_x2_74155_3: pin names not known; wires that end beside it: n2_to_4_decoder_x2_74155_3_p1, n2_to_4_decoder_x2_74155_3_p2, or_14_out, n2_to_4_decoder_x2_74155_3_p4, n2_to_4_decoder_x2_74155_3_p5, n2_to_4_decoder_x2_74155_3_p6, n2_to_4_decoder_x2_74155_3_p7, and_2_out
  not not_26 (not_26_out, n2_to_4_decoder_x2_74155_3_p2);
  not not_27 (not_27_out, n2_to_4_decoder_x2_74155_3_p4);
  not not_28 (not_28_out, n2_to_4_decoder_x2_74155_3_p6);
  not not_29 (not_29_out, n2_to_4_decoder_x2_74155_3_p5);
  xor xor_4 (n2_to_4_decoder_x2_74155_3_p1, B0, A0);
  not not_30 (n2_to_4_decoder_x2_74155_3_p7, and_2_out);
  and and_25 (B, and_9_out, or_17_out);
  and and_26 (and_26_out, not_11_out, A0);
  and and_27 (and_27_out, A1, B0);
  or or_17 (or_17_out, and_27_out, and_26_out);
  xnor xnor_1 (xnor_1_out, A1, B1);
  xnor xnor_2 (xnor_2_out, A0, B0);
  and and_28 (and_28_out, xnor_1_out, xnor_2_out);
  and and_29 (and_29_out, not_8_out, B1);
  // _2_to_4_Decoder__x2___74155 #(.Facing("south")) 2_to_4_decoder_x2_74155_4: pin names not known; wires that end beside it: and_28_out, n2_to_4_decoder_x2_74155_4_p2, n2_to_4_decoder_x2_74155_4_p3, n2_to_4_decoder_x2_74155_4_p4, n2_to_4_decoder_x2_74155_4_p5, n2_to_4_decoder_x2_74155_4_p6, and_10_out
  not not_31 (L, n2_to_4_decoder_x2_74155_4_p5);
  not not_32 (E, n2_to_4_decoder_x2_74155_4_p4);
  not not_33 (G, n2_to_4_decoder_x2_74155_4_p2);
  and and_30 (and_30_out, not_10_out, B0);
  and and_31 (and_31_out, and_30_out, B1);
  and and_32 (and_32_out, not_8_out, and_30_out);
  or or_18 (or_18_out, and_32_out, and_31_out);
  or or_19 (n2_to_4_decoder_x2_74155_4_p3, and_29_out, or_18_out);
  not not_34 (n2_to_4_decoder_x2_74155_4_p6, and_10_out);
endmodule
